# Fritzing sketch sketch (saved by Fritzing 0.9.6b)
breadboards: 1

parts:
  J1 = STM32 Nucleo boards  # not connected
  U1 = LIPO-1000mAh [package=lipo-1000]
  GSM_SIM_GPSR_SMS_SIM900_SIM1 = SIM800L [package=THT]

nets:
  N1: U1.+, GSM_SIM_GPSR_SMS_SIM900_SIM1.VDD
  N2: U1.-, GSM_SIM_GPSR_SMS_SIM900_SIM1.GND#1
